# Fritzing sketch openBeetle PCB CAN RTC GPS bulb out rev 11 (saved by Fritzing 0.7.12b)
breadboards: 1

parts:
  Q5 = Basic FET P-Channel [part_number=IRF9540PBF package="TO220 [THT]"]
  Q7 = Basic FET P-Channel [part_number=IRF9540PBF package="TO220 [THT]"]
  Q9 = Basic FET P-Channel [part_number=IRF9540PBF package="TO220 [THT]"]
  Q11 = Basic FET P-Channel [part_number=IRF9540PBF package="TO220 [THT]"]
  Q13 = Basic FET P-Channel [part_number=IRF9540PBF package="TO220 [THT]"]
  Q15 = Basic FET P-Channel [part_number=IRF9540PBF package="TO220 [THT]"]
  Q17 = Basic FET P-Channel [part_number=IRF9540PBF package="TO220 [THT]"]
  Q19 = Basic FET P-Channel [part_number=IRF9540PBF package="TO220 [THT]"]
  Q21 = Basic FET P-Channel [part_number=IRF9540PBF package="TO220 [THT]"]
  Q23 = Basic FET P-Channel [part_number=IRF9540PBF package="TO220 [THT]"]
  Q25 = Basic FET P-Channel [part_number=IRF9540PBF package="TO220 [THT]"]
  Q1 = Basic FET P-Channel [part_number=IRF9540PBF package="TO220 [THT]"]
  Q6 = NPN-Transistor [part_number=2N3904BU package="TO92 [THT]"]
  Q8 = NPN-Transistor [part_number=2N3904BU package="TO92 [THT]"]
  Q10 = NPN-Transistor [part_number=2N3904BU package="TO92 [THT]"]
  Q12 = NPN-Transistor [part_number=2N3904BU package="TO92 [THT]"]
  Q16 = NPN-Transistor [part_number=2N3904BU package="TO92 [THT]"]
  Q3 = Basic FET P-Channel [part_number=IRF9540PBF package="TO220 [THT]"]
  Q18 = NPN-Transistor [part_number=2N3904BU package="TO92 [THT]"]
  Q20 = NPN-Transistor [part_number=2N3904BU package="TO92 [THT]"]
  Q22 = NPN-Transistor [part_number=2N3904BU package="TO92 [THT]"]
  Q24 = NPN-Transistor [part_number=2N3904BU package="TO92 [THT]"]
  Q26 = NPN-Transistor [part_number=2N3904BU package="TO92 [THT]"]
  Q4 = NPN-Transistor [part_number=2N3904BU package="TO92 [THT]"]
  Q2 = NPN-Transistor [part_number=2N3904BU package="TO92 [THT]"]
  Q27 = Basic FET P-Channel [part_number=IRF9540PBF package="TO220 [THT]"]
  Q28 = NPN-Transistor [part_number=2N3904BU package="TO92 [THT]"]
  Q29 = Basic FET P-Channel [part_number=IRF9540PBF package="TO220 [THT]"]
  Q30 = NPN-Transistor [part_number=2N3904BU package="TO92 [THT]"]
  U2 = Voltage Regulator - 5V [part_number=L7805CV-DG package="TO220 [THT]"]  # not connected
  VinC7 = Electrolytic Capacitor [capacitance=1µF package="100 mil [THT, electrolytic]"]
  VinC8 = Electrolytic Capacitor [capacitance=1µF package="100 mil [THT, electrolytic]"]
  VinC9 = Electrolytic Capacitor [capacitance=1µF package="100 mil [THT, electrolytic]"]
  VinC1 = Electrolytic Capacitor [capacitance=1µF package="100 mil [THT, electrolytic]"]
  VinC2 = Electrolytic Capacitor [capacitance=1µF package="100 mil [THT, electrolytic]"]
  VinC3 = Electrolytic Capacitor [capacitance=1µF package="100 mil [THT, electrolytic]"]
  Input = screw terminal, 16 pins
  Arduino_MEGA_2560 = Arduino Mega
  J1 = screw terminal, 12 pins
  CAN = IC, DIP package, 18 pins [chip_label=IC spacing=300mil part_number=MCP2510-E/P]
  J2 = Screw terminal - 2 pins [package=THT]
  XTAL1 = Crystal [frequency="16 Mhz" package=THT]
  C1 = Ceramic Capacitor [capacitance=100nF package="100 mil [THT, multilayer]"]
  C2 = Ceramic Capacitor [capacitance=100nF package="100 mil [THT, multilayer]"]
  RTC = IC, DIP package, 24 pins [chip_label=IC spacing=300mil part_number=M41T00CAPPC1]
  IC1 = IC, SIP package, 8 pins [chip_label=IC spacing=300mil]
  IC2 = IC, SIP package, 8 pins [chip_label=IC spacing=300mil]
  D1 = Rectifier Diode [part_number=1N4001 package="Melf DO-213 AB [SMD]"]
  D2 = Rectifier Diode [part_number=1N4001 package="Melf DO-213 AB [SMD]"]
  D3 = Rectifier Diode [part_number=1N4001 package="Melf DO-213 AB [SMD]"]
  D4 = Rectifier Diode [part_number=1N4001 package="Melf DO-213 AB [SMD]"]
  D5 = Rectifier Diode [part_number=1N4001 package="Melf DO-213 AB [SMD]"]
  R37 = Resistor [tolerance=±1% resistance=10k package="1206 [SMD]"]
  R38 = Resistor [tolerance=±1% resistance=10k package="1206 [SMD]"]
  D6 = Rectifier Diode [part_number=1N4001 package="Melf DO-213 AB [SMD]"]
  R40 = Resistor [tolerance=±5% resistance=220 package="1206 [SMD]"]  # not connected
  R41 = Resistor [tolerance=±1% resistance=10k package="1206 [SMD]"]
  R42 = Resistor [tolerance=±1% resistance=10k package="1206 [SMD]"]
  D7 = Rectifier Diode [part_number=1N4001 package="Melf DO-213 AB [SMD]"]
  R44 = Resistor [tolerance=±1% resistance=10k package="1206 [SMD]"]
  R45 = Resistor [tolerance=±1% resistance=10k package="1206 [SMD]"]
  D8 = Rectifier Diode [part_number=1N4001 package="Melf DO-213 AB [SMD]"]
  D9 = Rectifier Diode [part_number=1N4001 package="Melf DO-213 AB [SMD]"]
  D10 = Rectifier Diode [part_number=1N4001 package="Melf DO-213 AB [SMD]"]
  D11 = Rectifier Diode [part_number=1N4001 package="Melf DO-213 AB [SMD]"]
  D12 = Rectifier Diode [part_number=1N4001 package="Melf DO-213 AB [SMD]"]
  D14 = Rectifier Diode [part_number=1N4001 package="Melf DO-213 AB [SMD]"]
  D15 = Rectifier Diode [part_number=1N4001 package="Melf DO-213 AB [SMD]"]
  D13 = Rectifier Diode [part_number=1N4001 package="Melf DO-213 AB [SMD]"]
  R50 = Resistor [tolerance=±5% resistance=220 package="1206 [SMD]"]
  R51 = Resistor [tolerance=±5% resistance=220 package="1206 [SMD]"]
  5VC1 = Electrolytic Capacitor [capacitance=100µF package="100 mil [THT, electrolytic]"]
  5VC2 = Electrolytic Capacitor [capacitance=100µF package="100 mil [THT, electrolytic]"]
  R4 = Resistor [tolerance=±1% resistance=10k package="0603 [SMD]"]
  R19 = Resistor [tolerance=±1% resistance=220 package="0603 [SMD]"]
  Q14 = NPN-Transistor [part_number=2N3904BU package="TO92 [THT]"]
  R22 = Resistor [tolerance=±1% resistance=10k package="0603 [SMD]"]
  R1 = Resistor [tolerance=±1% resistance=10k package="0603 [SMD]"]
  R52 = Resistor [tolerance=±5% resistance=220 package="0603 [SMD]"]
  R7 = Resistor [tolerance=±1% resistance=10k package="0603 [SMD]"]
  R8 = Resistor [tolerance=±1% resistance=10k package="0603 [SMD]"]
  R53 = Resistor [tolerance=±1% resistance=10k package="0603 [SMD]"]
  R10 = Resistor [tolerance=±1% resistance=10k package="0603 [SMD]"]
  R11 = Resistor [tolerance=±1% resistance=10k package="0603 [SMD]"]
  R13 = Resistor [tolerance=±1% resistance=10k package="0603 [SMD]"]
  R14 = Resistor [tolerance=±1% resistance=10k package="0603 [SMD]"]
  R16 = Resistor [tolerance=±1% resistance=10k package="0603 [SMD]"]
  R17 = Resistor [tolerance=±1% resistance=10k package="0603 [SMD]"]
  R20 = Resistor [tolerance=±1% resistance=10k package="0603 [SMD]"]
  R23 = Resistor [tolerance=±1% resistance=10k package="0603 [SMD]"]
  R25 = Resistor [tolerance=±1% resistance=10k package="0603 [SMD]"]
  R26 = Resistor [tolerance=±1% resistance=10k package="0603 [SMD]"]
  R28 = Resistor [tolerance=±1% resistance=10k package="0603 [SMD]"]
  R29 = Resistor [tolerance=±1% resistance=10k package="0603 [SMD]"]
  R31 = Resistor [tolerance=±1% resistance=10k package="0603 [SMD]"]
  R32 = Resistor [tolerance=±1% resistance=10k package="0603 [SMD]"]
  R34 = Resistor [tolerance=±1% resistance=10k package="0603 [SMD]"]
  R35 = Resistor [tolerance=±1% resistance=10k package="0603 [SMD]"]

nets:
  N1: Q5.gate, Q6.C, R7.Pin_0
  N2: Q5.drain, D13.anode
  N3: Q5.source, R7.Pin_1
  N4: Q7.gate, Q8.C, R10.Pin_0
  N5: Q7.drain, D12.anode
  N6: Q7.source, R10.Pin_1
  N7: Q9.gate, Q10.C, R13.Pin_0
  N8: Q9.drain, D11.anode
  N9: Q9.source, R13.Pin_1
  N10: Q11.gate, Q12.C, R16.Pin_0
  N11: Q11.drain, D10.anode
  N12: Q11.source, R16.Pin_1
  N13: Q13.gate, R19.Pin_0, Q14.C
  N14: Q13.drain, D9.anode
  N15: Q13.source, R19.Pin_1
  N16: Q15.gate, Q16.C, R22.Pin_0
  N17: Q15.drain, D1.anode
  N18: Q15.source, R22.Pin_1
  N19: Q17.gate, Q18.C, R25.Pin_0
  N20: Q17.drain, D2.anode
  N21: Q17.source, R25.Pin_1
  N22: Q19.gate, Q20.C, R28.Pin_0
  N23: Q19.drain, D3.anode
  N24: Q19.source, R28.Pin_1
  N25: Q21.gate, Q22.C, R31.Pin_0
  N26: Q21.drain, D4.anode
  N27: Q21.source, R31.Pin_1
  N28: Q23.gate, Q24.C, R34.Pin_0
  N29: Q23.drain, D5.anode
  N30: Q23.source, R34.Pin_1
  N31: Q25.gate, Q26.C, R37.Pin_0
  N32: Q25.drain, D6.anode
  N33: Q25.source, R37.Pin_1
  N34: Q1.gate, Q2.C, R1.Pin_0
  N35: Q1.drain, D15.anode
  N36: Q1.source, R1.Pin_1
  N37: Q6.B, R8.Pin_0
  N38: Q8.B, R11.Pin_0
  N39: Q10.B, R14.Pin_0
  N40: Q12.B, R17.Pin_0
  N41: Q16.B, R23.Pin_0
  N42: Q3.gate, Q4.C, R4.Pin_0
  N43: Q3.drain, D14.anode
  N44: Q3.source, R4.Pin_1
  N45: Q18.B, R26.Pin_0
  N46: Q20.B, R29.Pin_0
  N47: Q22.B, R32.Pin_0
  N48: Q24.B, R35.Pin_0
  N49: Q26.B, R38.Pin_0
  N50: Q4.B, R53.Pin_0
  N51: Q2.B, R52.Pin_1
  N52: Q27.gate, Q28.C, R41.Pin_0
  N53: Q27.drain, D7.anode
  N54: Q27.source, R41.Pin_1
  N55: Q28.B, R42.Pin_0
  N56: Q29.gate, Q30.C, R44.Pin_0
  N57: Q29.drain, D8.anode
  N58: Q29.source, R44.Pin_1
  N59: Q30.B, R45.Pin_0
  N60: VinC7.-, VinC8.-, VinC9.-, Input.pin1, Arduino_MEGA_2560.GND, J1.pin1, C1.0, C2.1, RTC.pin24, IC2.pin7
  N61: VinC7.+, VinC8.+, VinC9.+
  N62: VinC1.-, VinC2.-, VinC3.-
  N63: VinC1.+, VinC2.+, VinC3.+
  N64: Input.pin2, Arduino_MEGA_2560.D21, RTC.pin14, R50.Pin_0
  N65: Input.pin3, Arduino_MEGA_2560.D20, RTC.pin15, R51.Pin_0
  N66: Input.pin4, Arduino_MEGA_2560.A11
  N67: Input.pin5, Arduino_MEGA_2560.A10
  N68: Input.pin6, Arduino_MEGA_2560.A9
  N69: Input.pin7, Arduino_MEGA_2560.A8
  N70: Input.pin8, Arduino_MEGA_2560.A7
  N71: Input.pin9, Arduino_MEGA_2560.A6
  N72: Input.pin10, Arduino_MEGA_2560.A5
  N73: Input.pin11, Arduino_MEGA_2560.A4
  N74: Input.pin12, Arduino_MEGA_2560.A3
  N75: Input.pin13, Arduino_MEGA_2560.A2
  N76: Input.pin14, Arduino_MEGA_2560.A1
  N77: Input.pin15, Arduino_MEGA_2560.A0
  N78: Input.pin16, Arduino_MEGA_2560.VIN, R50.Pin_1, R51.Pin_1, 5VC1.+, 5VC2.+
  N79: Arduino_MEGA_2560.D13, R52.Pin_0
  N80: Arduino_MEGA_2560.D12, R53.Pin_1
  N81: Arduino_MEGA_2560.D11, R8.Pin_1
  N82: Arduino_MEGA_2560.D10, R11.Pin_1
  N83: Arduino_MEGA_2560.D9, R14.Pin_1
  N84: Arduino_MEGA_2560.D8, R17.Pin_1
  N85: Arduino_MEGA_2560.D7, R20.Pin_1
  N86: Arduino_MEGA_2560.D6, R23.Pin_1
  N87: Arduino_MEGA_2560.D5, R26.Pin_1
  N88: Arduino_MEGA_2560.D4, R29.Pin_1
  N89: Arduino_MEGA_2560.D3, R32.Pin_1
  N90: Arduino_MEGA_2560.D2, R35.Pin_1
  N91: Arduino_MEGA_2560.3V3, IC1.pin8
  N92: Arduino_MEGA_2560.D24, J1.pin12
  N93: Arduino_MEGA_2560.D26, J1.pin11
  N94: Arduino_MEGA_2560.D28, J1.pin10
  N95: Arduino_MEGA_2560.D30, J1.pin9
  N96: Arduino_MEGA_2560.D32, J1.pin8
  N97: Arduino_MEGA_2560.D34, J1.pin7
  N98: Arduino_MEGA_2560.D36, J1.pin6
  N99: Arduino_MEGA_2560.D38, J1.pin5
  N100: Arduino_MEGA_2560.D40, J1.pin4
  N101: Arduino_MEGA_2560.D42, J1.pin3
  N102: Arduino_MEGA_2560.D48, J1.pin2
  N103: Arduino_MEGA_2560.D50, CAN.pin15, IC1.pin2
  N104: Arduino_MEGA_2560.D51, CAN.pin14, IC1.pin1
  N105: Arduino_MEGA_2560.D52, CAN.pin13, IC1.pin3
  N106: Arduino_MEGA_2560.D53, CAN.pin16, IC1.pin4
  N107: Arduino_MEGA_2560.+5V#80, CAN.pin18, RTC.pin12
  N108: CAN.pin1, J2.pin1
  N109: CAN.pin2, J2.pin2
  N110: CAN.pin7, XTAL1.pin_1, C2.0
  N111: CAN.pin8, XTAL1.pin_0, C1.1
  N112: 5VC1.-, 5VC2.-
  N113: Q14.B, R20.Pin_0

notes:
  openBeetle Project
  Prototype 01
  Built For Tracy Young
  1961 VW Beetle
  April 2013 Calgary AB
  452 holes old
  relocate I2C to otherside of header
