# Fritzing sketch openBeetle PCB CAN RTC GPS bulb out rev 12 (saved by Fritzing 0.7.12b)
breadboards: 1

parts:
  Q5 = Basic FET P-Channel [part_number=IRF9540PBF package="TO220 [THT]"]
  Q7 = Basic FET P-Channel [part_number=IRF9540PBF package="TO220 [THT]"]
  Q9 = Basic FET P-Channel [part_number=IRF9540PBF package="TO220 [THT]"]
  Q11 = Basic FET P-Channel [part_number=IRF9540PBF package="TO220 [THT]"]
  Q13 = Basic FET P-Channel [part_number=IRF9540PBF package="TO220 [THT]"]
  Q15 = Basic FET P-Channel [part_number=IRF9540PBF package="TO220 [THT]"]
  Q17 = Basic FET P-Channel [part_number=IRF9540PBF package="TO220 [THT]"]
  Q19 = Basic FET P-Channel [part_number=IRF9540PBF package="TO220 [THT]"]
  Q21 = Basic FET P-Channel [part_number=IRF9540PBF package="TO220 [THT]"]
  Q23 = Basic FET P-Channel [part_number=IRF9540PBF package="TO220 [THT]"]
  Q25 = Basic FET P-Channel [part_number=IRF9540PBF package="TO220 [THT]"]
  Q1 = Basic FET P-Channel [part_number=IRF9540PBF package="TO220 [THT]"]
  Q6 = NPN-Transistor [part_number=2N3904BU package="TO92 [THT]"]
  Q8 = NPN-Transistor [part_number=2N3904BU package="TO92 [THT]"]
  Q10 = NPN-Transistor [part_number=2N3904BU package="TO92 [THT]"]
  Q12 = NPN-Transistor [part_number=2N3904BU package="TO92 [THT]"]
  Q16 = NPN-Transistor [part_number=2N3904BU package="TO92 [THT]"]
  Q3 = Basic FET P-Channel [part_number=IRF9540PBF package="TO220 [THT]"]
  Q18 = NPN-Transistor [part_number=2N3904BU package="TO92 [THT]"]
  Q20 = NPN-Transistor [part_number=2N3904BU package="TO92 [THT]"]
  Q22 = NPN-Transistor [part_number=2N3904BU package="TO92 [THT]"]
  Q24 = NPN-Transistor [part_number=2N3904BU package="TO92 [THT]"]
  Q26 = NPN-Transistor [part_number=2N3904BU package="TO92 [THT]"]
  Q4 = NPN-Transistor [part_number=2N3904BU package="TO92 [THT]"]
  Q2 = NPN-Transistor [part_number=2N3904BU package="TO92 [THT]"]
  Q27 = Basic FET P-Channel [part_number=IRF9540PBF package="TO220 [THT]"]
  Q28 = NPN-Transistor [part_number=2N3904BU package="TO92 [THT]"]
  Q29 = Basic FET P-Channel [part_number=IRF9540PBF package="TO220 [THT]"]
  Q30 = NPN-Transistor [part_number=2N3904BU package="TO92 [THT]"]
  VinC1 = Electrolytic Capacitor [capacitance=1µF package="100 mil [THT, electrolytic]"]
  Arduino_MEGA_2560 = Arduino Mega
  J1 = screw terminal, 12 pins
  CAN = IC, DIP package, 18 pins [chip_label=IC spacing=300mil part_number=MCP2510-E/P]
  XTAL1 = Crystal [frequency="16 Mhz" package=THT]
  C1 = Ceramic Capacitor [capacitance=100nF package="100 mil [THT, multilayer]"]
  C2 = Ceramic Capacitor [capacitance=100nF package="100 mil [THT, multilayer]"]
  RTC = IC, DIP package, 24 pins [chip_label=IC spacing=300mil part_number=M41T00CAPPC1]
  IC1 = IC, SIP package, 8 pins [chip_label=IC spacing=300mil]
  IC2 = IC, SIP package, 8 pins [chip_label=IC spacing=300mil]
  D1 = Rectifier Diode [part_number=1N4001 package="Melf DO-213 AB [SMD]"]
  D2 = Rectifier Diode [part_number=1N4001 package="Melf DO-213 AB [SMD]"]
  D3 = Rectifier Diode [part_number=1N4001 package="Melf DO-213 AB [SMD]"]
  D4 = Rectifier Diode [part_number=1N4001 package="Melf DO-213 AB [SMD]"]
  D5 = Rectifier Diode [part_number=1N4001 package="Melf DO-213 AB [SMD]"]
  D6 = Rectifier Diode [part_number=1N4001 package="Melf DO-213 AB [SMD]"]
  D7 = Rectifier Diode [part_number=1N4001 package="Melf DO-213 AB [SMD]"]
  D8 = Rectifier Diode [part_number=1N4001 package="Melf DO-213 AB [SMD]"]
  D9 = Rectifier Diode [part_number=1N4001 package="Melf DO-213 AB [SMD]"]
  D10 = Rectifier Diode [part_number=1N4001 package="Melf DO-213 AB [SMD]"]
  D11 = Rectifier Diode [part_number=1N4001 package="Melf DO-213 AB [SMD]"]
  D12 = Rectifier Diode [part_number=1N4001 package="Melf DO-213 AB [SMD]"]
  D14 = Rectifier Diode [part_number=1N4001 package="Melf DO-213 AB [SMD]"]
  D15 = Rectifier Diode [part_number=1N4001 package="Melf DO-213 AB [SMD]"]
  D13 = Rectifier Diode [part_number=1N4001 package="Melf DO-213 AB [SMD]"]
  R4 = Resistor [tolerance=±1% resistance=10k package="0603 [SMD]"]
  R19 = Resistor [tolerance=±1% resistance=220 package="0603 [SMD]"]
  Q14 = NPN-Transistor [part_number=2N3904BU package="TO92 [THT]"]
  R22 = Resistor [tolerance=±1% resistance=10k package="0603 [SMD]"]
  R1 = Resistor [tolerance=±1% resistance=10k package="0603 [SMD]"]
  R52 = Resistor [tolerance=±5% resistance=220 package="0603 [SMD]"]
  R7 = Resistor [tolerance=±1% resistance=10k package="0603 [SMD]"]
  R8 = Resistor [tolerance=±1% resistance=10k package="0603 [SMD]"]
  R53 = Resistor [tolerance=±1% resistance=10k package="0603 [SMD]"]
  R10 = Resistor [tolerance=±1% resistance=10k package="0603 [SMD]"]
  R11 = Resistor [tolerance=±1% resistance=10k package="0603 [SMD]"]
  R13 = Resistor [tolerance=±1% resistance=10k package="0603 [SMD]"]
  R14 = Resistor [tolerance=±1% resistance=10k package="0603 [SMD]"]
  R16 = Resistor [tolerance=±1% resistance=10k package="0603 [SMD]"]
  R17 = Resistor [tolerance=±1% resistance=10k package="0603 [SMD]"]
  R20 = Resistor [tolerance=±1% resistance=10k package="0603 [SMD]"]
  R23 = Resistor [tolerance=±1% resistance=10k package="0603 [SMD]"]
  R25 = Resistor [tolerance=±1% resistance=10k package="0603 [SMD]"]
  R26 = Resistor [tolerance=±1% resistance=10k package="0603 [SMD]"]
  R28 = Resistor [tolerance=±1% resistance=10k package="0603 [SMD]"]
  R29 = Resistor [tolerance=±1% resistance=10k package="0603 [SMD]"]
  R31 = Resistor [tolerance=±1% resistance=10k package="0603 [SMD]"]
  R32 = Resistor [tolerance=±1% resistance=10k package="0603 [SMD]"]
  R34 = Resistor [tolerance=±1% resistance=10k package="0603 [SMD]"]
  R35 = Resistor [tolerance=±1% resistance=10k package="0603 [SMD]"]
  R37 = Resistor [tolerance=±1% resistance=10k package="0603 [SMD]"]
  R38 = Resistor [tolerance=±1% resistance=10k package="0603 [SMD]"]
  R41 = Resistor [tolerance=±1% resistance=10k package="0603 [SMD]"]
  R42 = Resistor [tolerance=±1% resistance=10k package="0603 [SMD]"]
  R44 = Resistor [tolerance=±1% resistance=10k package="0603 [SMD]"]
  R45 = Resistor [tolerance=±1% resistance=10k package="0603 [SMD]"]
  U1 = Voltage Regulator - 5V [package="DPak [SMD]"]
  J3 = screw terminal, 20 pins
  VinC2 = Electrolytic Capacitor [capacitance=1µF package="100 mil [THT, electrolytic]"]
  VinC3 = Electrolytic Capacitor [capacitance=1µF package="100 mil [THT, electrolytic]"]
  R55 = Resistor [tolerance=±5% resistance=220 package="0603 [SMD]"]
  R56 = Resistor [tolerance=±5% resistance=220 package="0603 [SMD]"]
  C3 = Electrolytic Capacitor [capacitance=1µF package="100 mil [THT, electrolytic]"]
  C4 = Electrolytic Capacitor [capacitance=1µF package="100 mil [THT, electrolytic]"]

nets:
  N1: Q5.gate, Q6.C, R7.Pin_0
  N2: Q5.drain, D13.anode
  N3: Q5.source, Q7.source, Q9.source, Q11.source, Q13.source, Q15.source, Q17.source, Q19.source, Q21.source, Q23.source, Q25.source, Q1.source, Q3.source, Q27.source, Q29.source, VinC1.+, R4.Pin_1, R19.Pin_1, R22.Pin_1, R1.Pin_1, R7.Pin_1, R10.Pin_1, R13.Pin_1, R16.Pin_1, R25.Pin_1, R28.Pin_1, R31.Pin_1, R34.Pin_1, R37.Pin_1, R41.Pin_1, R44.Pin_1, U1.input_voltage, VinC2.+, VinC3.+, R56.Pin_0
  N4: Q7.gate, Q8.C, R10.Pin_0
  N5: Q7.drain, D12.anode
  N6: Q9.gate, Q10.C, R13.Pin_0
  N7: Q9.drain, D11.anode
  N8: Q11.gate, Q12.C, R16.Pin_0
  N9: Q11.drain, D10.anode
  N10: Q13.gate, R19.Pin_0, Q14.C
  N11: Q13.drain, D9.anode
  N12: Q15.gate, Q16.C, R22.Pin_0
  N13: Q15.drain, D1.anode
  N14: Q17.gate, Q18.C, R25.Pin_0
  N15: Q17.drain, D2.anode
  N16: Q19.gate, Q20.C, R28.Pin_0
  N17: Q19.drain, D3.anode
  N18: Q21.gate, Q22.C, R31.Pin_0
  N19: Q21.drain, D4.anode
  N20: Q23.gate, Q24.C, R34.Pin_0
  N21: Q23.drain, D5.anode
  N22: Q25.gate, Q26.C, R37.Pin_0
  N23: Q25.drain, D6.anode
  N24: Q1.gate, Q2.C, R1.Pin_0
  N25: Q1.drain, D15.anode
  GND: Q6.E, Q8.E, Q10.E, Q12.E, Q16.E, Q18.E, Q20.E, Q22.E, Q24.E, Q26.E, Q4.E, Q2.E, Q28.E, Q30.E, VinC1.-, Arduino_MEGA_2560.GND, J1.pin1, C1.0, C2.1, RTC.pin24, IC2.pin7, Q14.E, U1.GND, J3.pin20, VinC2.-, VinC3.-, R55.Pin_0, C3.-, C4.-
  N26: Q6.B, R8.Pin_0
  N27: Q8.B, R11.Pin_0
  N28: Q10.B, R14.Pin_0
  N29: Q12.B, R17.Pin_0
  N30: Q16.B, R23.Pin_0
  N31: Q3.gate, Q4.C, R4.Pin_0
  N32: Q3.drain, D14.anode
  N33: Q18.B, R26.Pin_0
  N34: Q20.B, R29.Pin_0
  N35: Q22.B, R32.Pin_0
  N36: Q24.B, R35.Pin_0
  N37: Q26.B, R38.Pin_0
  N38: Q4.B, R53.Pin_0
  N39: Q2.B, R52.Pin_1
  N40: Q27.gate, Q28.C, R41.Pin_0
  N41: Q27.drain, D7.anode
  N42: Q28.B, R42.Pin_0
  N43: Q29.gate, Q30.C, R44.Pin_0
  N44: Q29.drain, D8.anode
  N45: Q30.B, R45.Pin_0
  N46: Arduino_MEGA_2560.D13, R52.Pin_0
  N47: Arduino_MEGA_2560.D12, R53.Pin_1
  N48: Arduino_MEGA_2560.D11, R8.Pin_1
  N49: Arduino_MEGA_2560.D10, R11.Pin_1
  N50: Arduino_MEGA_2560.D9, R14.Pin_1
  N51: Arduino_MEGA_2560.D8, R17.Pin_1
  N52: Arduino_MEGA_2560.D7, R20.Pin_1
  N53: Arduino_MEGA_2560.D6, R23.Pin_1
  N54: Arduino_MEGA_2560.D5, R26.Pin_1
  N55: Arduino_MEGA_2560.D4, R29.Pin_1
  N56: Arduino_MEGA_2560.D3, R32.Pin_1
  N57: Arduino_MEGA_2560.D2, R35.Pin_1
  N58: Arduino_MEGA_2560.3V3, IC1.pin8
  N59: Arduino_MEGA_2560.VIN, U1.output_voltage, J3.pin19, C3.+, C4.+
  N60: Arduino_MEGA_2560.A0, J3.pin14
  N61: Arduino_MEGA_2560.A1, J3.pin13
  N62: Arduino_MEGA_2560.A2, J3.pin12
  N63: Arduino_MEGA_2560.A3, J3.pin11
  N64: Arduino_MEGA_2560.A4, J3.pin10
  N65: Arduino_MEGA_2560.A5, J3.pin9
  N66: Arduino_MEGA_2560.D20, RTC.pin15, J3.pin15
  N67: Arduino_MEGA_2560.D21, RTC.pin14, J3.pin16
  N68: Arduino_MEGA_2560.D22, D15.cathode
  N69: Arduino_MEGA_2560.D23, D13.cathode
  N70: Arduino_MEGA_2560.D24, J1.pin12
  N71: Arduino_MEGA_2560.D25, D12.cathode
  N72: Arduino_MEGA_2560.D26, J1.pin11
  N73: Arduino_MEGA_2560.D27, D11.cathode
  N74: Arduino_MEGA_2560.D28, J1.pin10
  N75: Arduino_MEGA_2560.D29, D10.cathode
  N76: Arduino_MEGA_2560.D30, J1.pin9
  N77: Arduino_MEGA_2560.D31, D9.cathode
  N78: Arduino_MEGA_2560.D32, J1.pin8
  N79: Arduino_MEGA_2560.D33, D1.cathode
  N80: Arduino_MEGA_2560.D34, J1.pin7
  N81: Arduino_MEGA_2560.D35, D2.cathode
  N82: Arduino_MEGA_2560.D36, J1.pin6
  N83: Arduino_MEGA_2560.D37, D3.cathode
  N84: Arduino_MEGA_2560.D38, J1.pin5
  N85: Arduino_MEGA_2560.D39, D4.cathode
  N86: Arduino_MEGA_2560.D40, J1.pin4
  N87: Arduino_MEGA_2560.D41, D5.cathode
  N88: Arduino_MEGA_2560.D42, J1.pin3
  N89: Arduino_MEGA_2560.D43, D6.cathode
  N90: Arduino_MEGA_2560.D44, R38.Pin_1
  N91: Arduino_MEGA_2560.D45, R42.Pin_1
  N92: Arduino_MEGA_2560.D46, R45.Pin_1
  N93: Arduino_MEGA_2560.D47, D7.cathode
  N94: Arduino_MEGA_2560.D48, J1.pin2
  N95: Arduino_MEGA_2560.D49, D8.cathode
  N96: Arduino_MEGA_2560.D50, CAN.pin15, IC1.pin2
  N97: Arduino_MEGA_2560.D51, CAN.pin14, IC1.pin1
  N98: Arduino_MEGA_2560.D52, CAN.pin13, IC1.pin3
  N99: Arduino_MEGA_2560.D53, CAN.pin16, IC1.pin4
  N100: Arduino_MEGA_2560.A6, J3.pin8
  N101: Arduino_MEGA_2560.A7, J3.pin7
  N102: Arduino_MEGA_2560.A8, J3.pin6
  N103: Arduino_MEGA_2560.A9, J3.pin5
  N104: Arduino_MEGA_2560.A10, J3.pin4
  N105: Arduino_MEGA_2560.A11, J3.pin3
  N106: Arduino_MEGA_2560.A12, J3.pin2
  N107: Arduino_MEGA_2560.A13, J3.pin1
  N108: Arduino_MEGA_2560.A15, R55.Pin_1, R56.Pin_1
  N109: Arduino_MEGA_2560.+5V#80, CAN.pin18, RTC.pin12
  N110: Arduino_MEGA_2560.+5V#81, D14.cathode
  N111: CAN.pin1, J3.pin17
  N112: CAN.pin2, J3.pin18
  N113: CAN.pin7, XTAL1.pin_1, C2.0
  N114: CAN.pin8, XTAL1.pin_0, C1.1
  N115: Q14.B, R20.Pin_0

notes:
  openBeetle Project
  Prototype 01
  Built For Tracy Young
  1961 VW Beetle
  April 2013 Calgary AB
