# Fritzing sketch openBeetle PCB CAN RTC GPS bulb out rev 15 bluetooth (saved by Fritzing 0.7.12b)
breadboards: 1

parts:
  Q5 = Basic FET P-Channel [part_number=IRF9540PBF package="TO220 [THT]"]
  Q7 = Basic FET P-Channel [part_number=IRF9540PBF package="TO220 [THT]"]
  Q9 = Basic FET P-Channel [part_number=IRF9540PBF package="TO220 [THT]"]
  Q11 = Basic FET P-Channel [part_number=IRF9540PBF package="TO220 [THT]"]
  Q13 = Basic FET P-Channel [part_number=IRF9540PBF package="TO220 [THT]"]
  Q15 = Basic FET P-Channel [part_number=IRF9540PBF package="TO220 [THT]"]
  Q17 = Basic FET P-Channel [part_number=IRF9540PBF package="TO220 [THT]"]
  Q19 = Basic FET P-Channel [part_number=IRF9540PBF package="TO220 [THT]"]
  Q21 = Basic FET P-Channel [part_number=IRF9540PBF package="TO220 [THT]"]
  Q23 = Basic FET P-Channel [part_number=IRF9540PBF package="TO220 [THT]"]
  Q25 = Basic FET P-Channel [part_number=IRF9540PBF package="TO220 [THT]"]
  Q1 = Basic FET P-Channel [part_number=IRF9540PBF package="TO220 [THT]"]
  Q6 = NPN-Transistor [part_number=2N3904BU package="TO92 [THT]"]
  Q8 = NPN-Transistor [part_number=2N3904BU package="TO92 [THT]"]
  Q10 = NPN-Transistor [part_number=2N3904BU package="TO92 [THT]"]
  Q12 = NPN-Transistor [part_number=2N3904BU package="TO92 [THT]"]
  Q16 = NPN-Transistor [part_number=2N3904BU package="TO92 [THT]"]
  Q3 = Basic FET P-Channel [part_number=IRF9540PBF package="TO220 [THT]"]
  Q18 = NPN-Transistor [part_number=2N3904BU package="TO92 [THT]"]
  Q20 = NPN-Transistor [part_number=2N3904BU package="TO92 [THT]"]
  Q22 = NPN-Transistor [part_number=2N3904BU package="TO92 [THT]"]
  Q24 = NPN-Transistor [part_number=2N3904BU package="TO92 [THT]"]
  Q26 = NPN-Transistor [part_number=2N3904BU package="TO92 [THT]"]
  Q4 = NPN-Transistor [part_number=2N3904BU package="TO92 [THT]"]
  Q2 = NPN-Transistor [part_number=2N3904BU package="TO92 [THT]"]
  Q27 = Basic FET P-Channel [part_number=IRF9540PBF package="TO220 [THT]"]
  Q28 = NPN-Transistor [part_number=2N3904BU package="TO92 [THT]"]
  Q29 = Basic FET P-Channel [part_number=IRF9540PBF package="TO220 [THT]"]
  Q30 = NPN-Transistor [part_number=2N3904BU package="TO92 [THT]"]
  VinC1 = Electrolytic Capacitor [capacitance=1µF package="100 mil [THT, electrolytic]"]
  Arduino_MEGA_2560 = Arduino Mega
  CAN = IC, DIP package, 18 pins [chip_label=IC spacing=300mil part_number=MCP2510-E/P]
  XTAL1 = Crystal [frequency="16 Mhz" package=THT]
  C2 = Ceramic Capacitor [capacitance=100nF package="100 mil [THT, multilayer]"]
  C1 = Ceramic Capacitor [capacitance=100nF package="100 mil [THT, multilayer]"]
  RTC = IC, DIP package, 24 pins [chip_label=IC spacing=300mil part_number=M41T00CAPPC1]
  GPS2 = IC, SIP package, 8 pins [chip_label=IC spacing=300mil]
  GPS1 = IC, SIP package, 8 pins [chip_label=IC spacing=300mil]
  D6 = Rectifier Diode [part_number=SGL41-20-E3/96 package="Melf DO-213 AB [SMD]"]
  R3 = Resistor [tolerance=±1% resistance=10k package="0603 [SMD]"]
  R13 = Resistor [tolerance=±1% resistance=220 package="0603 [SMD]"]
  Q14 = NPN-Transistor [part_number=2N3904BU package="TO92 [THT]"]
  R15 = Resistor [tolerance=±1% resistance=10k package="0603 [SMD]"]
  R1 = Resistor [tolerance=±1% resistance=10k part_number=MCT0603MC1002FP500 package="0603 [SMD]"]
  R2 = Resistor [tolerance=±5% resistance=220 package="0603 [SMD]"]
  R5 = Resistor [tolerance=±1% resistance=10k package="0603 [SMD]"]
  R6 = Resistor [tolerance=±1% resistance=10k package="0603 [SMD]"]
  R4 = Resistor [tolerance=±1% resistance=10k package="0603 [SMD]"]
  R7 = Resistor [tolerance=±1% resistance=10k package="0603 [SMD]"]
  R8 = Resistor [tolerance=±1% resistance=10k package="0603 [SMD]"]
  R9 = Resistor [tolerance=±1% resistance=10k package="0603 [SMD]"]
  R10 = Resistor [tolerance=±1% resistance=10k package="0603 [SMD]"]
  R11 = Resistor [tolerance=±1% resistance=10k package="0603 [SMD]"]
  R12 = Resistor [tolerance=±1% resistance=10k package="0603 [SMD]"]
  R14 = Resistor [tolerance=±1% resistance=10k package="0603 [SMD]"]
  R16 = Resistor [tolerance=±1% resistance=10k package="0603 [SMD]"]
  R17 = Resistor [tolerance=±1% resistance=10k package="0603 [SMD]"]
  R18 = Resistor [tolerance=±1% resistance=10k package="0603 [SMD]"]
  R19 = Resistor [tolerance=±1% resistance=10k package="0603 [SMD]"]
  R20 = Resistor [tolerance=±1% resistance=10k package="0603 [SMD]"]
  R21 = Resistor [tolerance=±1% resistance=10k package="0603 [SMD]"]
  R22 = Resistor [tolerance=±1% resistance=10k package="0603 [SMD]"]
  R23 = Resistor [tolerance=±1% resistance=10k package="0603 [SMD]"]
  R24 = Resistor [tolerance=±1% resistance=10k package="0603 [SMD]"]
  R25 = Resistor [tolerance=±1% resistance=10k package="0603 [SMD]"]
  R26 = Resistor [tolerance=±1% resistance=10k package="0603 [SMD]"]
  R27 = Resistor [tolerance=±1% resistance=10k package="0603 [SMD]"]
  R28 = Resistor [tolerance=±1% resistance=10k package="0603 [SMD]"]
  R29 = Resistor [tolerance=±1% resistance=10k package="0603 [SMD]"]
  R30 = Resistor [tolerance=±1% resistance=10k package="0603 [SMD]"]
  VinC2 = Electrolytic Capacitor [capacitance=1µF package="100 mil [THT, electrolytic]"]
  VinC3 = Electrolytic Capacitor [capacitance=1µF package="100 mil [THT, electrolytic]"]
  R32 = Resistor [tolerance=±5% resistance=220 package="0603 [SMD]"]
  R31 = Resistor [tolerance=±5% resistance=220 package="0603 [SMD]"]
  C3 = Electrolytic Capacitor [capacitance=1µF package="100 mil [THT, electrolytic]"]
  C4 = Electrolytic Capacitor [capacitance=1µF package="100 mil [THT, electrolytic]"]
  R33 = Resistor [tolerance=±5% resistance=220 package="0603 [SMD]"]
  R34 = Resistor [tolerance=±5% resistance=220 package="0603 [SMD]"]
  D1 = Schottky Diode [part_number=SGL41-20-E3/96 package="Melf DO-213 AB [SMD]"]
  D2 = Schottky Diode [part_number=SGL41-20-E3/96 package="Melf DO-213 AB [SMD]"]
  D3 = Schottky Diode [part_number=SGL41-20-E3/96 package="Melf DO-213 AB [SMD]"]
  D3_2 = Schottky Diode [part_number=SGL41-20-E3/96 package="Melf DO-213 AB [SMD]"]
  D4 = Schottky Diode [part_number=SGL41-20-E3/96 package="Melf DO-213 AB [SMD]"]
  D5 = Schottky Diode [part_number=SGL41-20-E3/96 package="Melf DO-213 AB [SMD]"]
  D7 = Schottky Diode [part_number=SGL41-20-E3/96 package="Melf DO-213 AB [SMD]"]
  D8 = Schottky Diode [part_number=SGL41-20-E3/96 package="Melf DO-213 AB [SMD]"]
  D3_3 = Schottky Diode [part_number=SGL41-20-E3/96 package="Melf DO-213 AB [SMD]"]
  D4_2 = Schottky Diode [part_number=SGL41-20-E3/96 package="Melf DO-213 AB [SMD]"]
  D5_2 = Schottky Diode [part_number=SGL41-20-E3/96 package="Melf DO-213 AB [SMD]"]
  D6_2 = Schottky Diode [part_number=SGL41-20-E3/96 package="Melf DO-213 AB [SMD]"]
  D7_2 = Schottky Diode [part_number=SGL41-20-E3/96 package="Melf DO-213 AB [SMD]"]
  D8_2 = Schottky Diode [part_number=SGL41-20-E3/96 package="Melf DO-213 AB [SMD]"]
  U2 = Voltage Regulator - 5V [part_number=KF50BDT-TR package="DPak [SMD]"]
  U3 = Voltage Regulator - 5V [part_number=KF50BDT-TR package="DPak [SMD]"]
  J4 = screw terminal, 12 pins
  J3 = screw terminal, 12 pins
  D_I/O = screw terminal, 16 pins
  Pad2 = Pad [width=0.8 height=1.3 connect=center]  # not connected
  Pad3 = Pad [width=0.8 height=1.3 connect=center]  # not connected
  Pad4 = Pad [width=0.8 height=1.3 connect=center]  # not connected
  Pad5 = Pad [width=0.8 height=1.3 connect=center]  # not connected
  Pad6 = Pad [width=0.8 height=1.3 connect=center]  # not connected
  Pad7 = Pad [width=0.8 height=1.3 connect=center]  # not connected
  Pad8 = Pad [width=0.8 height=1.3 connect=center]  # not connected
  Pad9 = Pad [width=0.8 height=1.3 connect=center]  # not connected
  Pad10 = Pad [width=0.8 height=1.3 connect=center]  # not connected
  Pad11 = Pad [width=0.8 height=1.3 connect=center]  # not connected
  Pad12 = Pad [width=0.8 height=1.3 connect=center]
  Pad13 = Pad [width=0.8 height=1.3 connect=center]
  Pad14 = Pad [width=0.8 height=1.3 connect=center]  # not connected
  Pad15 = Pad [width=0.8 height=1.3 connect=center]  # not connected
  Pad16 = Pad [width=0.8 height=1.3 connect=center]  # not connected
  Pad17 = Pad [width=0.8 height=1.3 connect=center]  # not connected
  Pad18 = Pad [width=0.8 height=1.3 connect=center]  # not connected
  Pad19 = Pad [width=0.8 height=1.3 connect=center]  # not connected
  Pad20 = Pad [width=0.8 height=1.3 connect=center]  # not connected
  Pad21 = Pad [width=0.8 height=1.3 connect=center]  # not connected
  Pad22 = Pad [width=0.8 height=1.3 connect=center]  # not connected
  Pad23 = Pad [width=0.8 height=1.3 connect=center]  # not connected
  Pad24 = Pad [width=0.8 height=1.3 connect=center]
  Pad25 = Pad [width=0.8 height=1.3 connect=center]
  R36 = Resistor [tolerance=±1% resistance=10k package="0603 [SMD]"]

nets:
  N1: Q5.gate, Q6.C, R5.Pin_0
  N2: Q5.drain, D3.anode
  N3: Q5.source, Q7.source, Q9.source, Q11.source, Q13.source, Q15.source, Q17.source, Q19.source, Q21.source, Q23.source, Q25.source, Q1.source, Q3.source, Q27.source, Q29.source, VinC1.+, R3.Pin_1, R13.Pin_1, R15.Pin_1, R1.Pin_1, R5.Pin_1, R7.Pin_1, R9.Pin_1, R11.Pin_1, R17.Pin_1, R19.Pin_1, R21.Pin_1, R23.Pin_1, R25.Pin_1, R27.Pin_1, R29.Pin_1, VinC2.+, VinC3.+, R32.Pin_0, U2.input_voltage, U3.input_voltage
  N4: Q7.gate, Q8.C, R7.Pin_0
  N5: Q7.drain, D3_2.anode
  N6: Q9.gate, Q10.C, R9.Pin_0
  N7: Q9.drain, D4.anode
  N8: Q11.gate, Q12.C, R11.Pin_0
  N9: Q11.drain, D5.anode
  N10: Q13.gate, R13.Pin_0, Q14.C
  N11: Q13.drain, D6.anode
  N12: Q15.gate, Q16.C, R15.Pin_0
  N13: Q15.drain, D7.anode
  N14: Q17.gate, Q18.C, R17.Pin_0
  N15: Q17.drain, D8.anode
  N16: Q19.gate, Q20.C, R19.Pin_0
  N17: Q19.drain, D3_3.anode
  N18: Q21.gate, Q22.C, R21.Pin_0
  N19: Q21.drain, D4_2.anode
  N20: Q23.gate, Q24.C, R23.Pin_0
  N21: Q23.drain, D5_2.anode
  N22: Q25.gate, Q26.C, R25.Pin_0
  N23: Q25.drain, D6_2.anode
  N24: Q1.gate, Q2.C, R1.Pin_0
  N25: Q1.drain, D1.anode
  GND: Q6.E, Q8.E, Q10.E, Q12.E, Q16.E, Q18.E, Q20.E, Q22.E, Q24.E, Q26.E, Q4.E, Q2.E, Q28.E, Q30.E, VinC1.-, Arduino_MEGA_2560.GND, C2.1, C1.0, RTC.pin24, GPS1.pin7, Q14.E, VinC2.-, VinC3.-, R31.Pin_0, C3.-, C4.-, U2.GND, U3.GND, J3.pin12, Pad25.pad
  N26: Q6.B, R6.Pin_0
  N27: Q8.B, R8.Pin_0
  N28: Q10.B, R10.Pin_0
  N29: Q12.B, R12.Pin_0
  N30: Q16.B, R16.Pin_0
  N31: Q3.gate, Q4.C, R3.Pin_0
  N32: Q3.drain, D2.anode
  N33: Q18.B, R18.Pin_0
  N34: Q20.B, R20.Pin_0
  N35: Q22.B, R22.Pin_0
  N36: Q24.B, R24.Pin_0
  N37: Q26.B, R26.Pin_0
  N38: Q4.B, R4.Pin_0
  N39: Q2.B, R2.Pin_1
  N40: Q27.gate, Q28.C, R27.Pin_0
  N41: Q27.drain, D7_2.anode
  N42: Q28.B, R28.Pin_0
  N43: Q29.gate, Q30.C, R29.Pin_0
  N44: Q29.drain, D8_2.anode
  N45: Q30.B, R30.Pin_0
  N46: Arduino_MEGA_2560.D13, R2.Pin_0
  N47: Arduino_MEGA_2560.D12, R4.Pin_1
  N48: Arduino_MEGA_2560.D11, R6.Pin_1
  N49: Arduino_MEGA_2560.D10, R8.Pin_1
  N50: Arduino_MEGA_2560.D9, R10.Pin_1
  N51: Arduino_MEGA_2560.D8, R12.Pin_1
  N52: Arduino_MEGA_2560.D7, R14.Pin_1
  N53: Arduino_MEGA_2560.D6, R16.Pin_1
  N54: Arduino_MEGA_2560.D5, R18.Pin_1
  N55: Arduino_MEGA_2560.D4, R20.Pin_1
  N56: Arduino_MEGA_2560.D3, R22.Pin_1
  N57: Arduino_MEGA_2560.D2, R24.Pin_1
  N58: Arduino_MEGA_2560.D1TX, Pad12.pad
  N59: Arduino_MEGA_2560.D0RX, Pad13.pad
  N60: Arduino_MEGA_2560.3V3, GPS2.pin8, Pad24.pad
  N61: Arduino_MEGA_2560.VIN, C3.+, C4.+, U2.output_voltage, U3.output_voltage, J3.pin11, R36.Pin_0, R36.Pin_1
  N62: Arduino_MEGA_2560.A0, J3.pin3
  N63: Arduino_MEGA_2560.A1, J3.pin2
  N64: Arduino_MEGA_2560.A2, J3.pin1
  N65: Arduino_MEGA_2560.A3, J4.pin12
  N66: Arduino_MEGA_2560.A4, J4.pin11
  N67: Arduino_MEGA_2560.A5, J4.pin10
  N68: Arduino_MEGA_2560.D20, RTC.pin15, R34.Pin_1, D_I/O.pin15
  N69: Arduino_MEGA_2560.D21, RTC.pin14, R33.Pin_1, D_I/O.pin16
  N70: Arduino_MEGA_2560.D22, D2.cathode
  N71: Arduino_MEGA_2560.D23, D3.cathode
  N72: Arduino_MEGA_2560.D24, D1.cathode
  N73: Arduino_MEGA_2560.D25, D3_2.cathode
  N74: Arduino_MEGA_2560.D26, D_I/O.pin3
  N75: Arduino_MEGA_2560.D27, D4.cathode
  N76: Arduino_MEGA_2560.D28, D_I/O.pin2
  N77: Arduino_MEGA_2560.D29, D5.cathode
  N78: Arduino_MEGA_2560.D30, D_I/O.pin1
  N79: Arduino_MEGA_2560.D31, D6.cathode
  N80: Arduino_MEGA_2560.D32, J3.pin10
  N81: Arduino_MEGA_2560.D33, D7.cathode
  N82: Arduino_MEGA_2560.D34, J3.pin9
  N83: Arduino_MEGA_2560.D35, D8.cathode
  N84: Arduino_MEGA_2560.D36, J3.pin8
  N85: Arduino_MEGA_2560.D37, D3_3.cathode
  N86: Arduino_MEGA_2560.D38, J3.pin7
  N87: Arduino_MEGA_2560.D39, D4_2.cathode
  N88: Arduino_MEGA_2560.D40, J3.pin6
  N89: Arduino_MEGA_2560.D41, D5_2.cathode
  N90: Arduino_MEGA_2560.D42, J3.pin5
  N91: Arduino_MEGA_2560.D43, D6_2.cathode
  N92: Arduino_MEGA_2560.D44, R26.Pin_1
  N93: Arduino_MEGA_2560.D45, R28.Pin_1
  N94: Arduino_MEGA_2560.D46, R30.Pin_1
  N95: Arduino_MEGA_2560.D47, D7_2.cathode
  N96: Arduino_MEGA_2560.D48, J3.pin4
  N97: Arduino_MEGA_2560.D49, D8_2.cathode
  N98: Arduino_MEGA_2560.D50, CAN.pin15, GPS2.pin2
  N99: Arduino_MEGA_2560.D51, CAN.pin14, GPS2.pin1
  N100: Arduino_MEGA_2560.D52, CAN.pin13, GPS2.pin3
  N101: Arduino_MEGA_2560.D53, CAN.pin16, GPS2.pin4
  N102: Arduino_MEGA_2560.A6, J4.pin9
  N103: Arduino_MEGA_2560.A7, J4.pin8
  N104: Arduino_MEGA_2560.A8, J4.pin7
  N105: Arduino_MEGA_2560.A9, J4.pin6
  N106: Arduino_MEGA_2560.A10, J4.pin5
  N107: Arduino_MEGA_2560.A11, J4.pin4
  N108: Arduino_MEGA_2560.A12, J4.pin3
  N109: Arduino_MEGA_2560.A13, J4.pin2
  N110: Arduino_MEGA_2560.A14, J4.pin1
  N111: Arduino_MEGA_2560.A15, R32.Pin_1, R31.Pin_1
  N112: Arduino_MEGA_2560.+5V, CAN.pin18, RTC.pin12, R33.Pin_0, R34.Pin_0
  N113: CAN.pin1, D_I/O.pin14
  N114: CAN.pin2, D_I/O.pin13
  N115: CAN.pin7, XTAL1.pin_1, C2.0
  N116: CAN.pin8, XTAL1.pin_0, C1.1
  N117: Q14.B, R14.Pin_0

notes:
  openBeetle Project
  Built For Tracy Young
  1961 VW Beetle
  Prototype 01
  April 2013 Calgary AB
